# Fritzing sketch sketch (saved by Fritzing 0.9.9b)
circuit board: 6.3cm x 6.3cm
breadboards: 2

parts:
  LED3 = smd LED [color="Red (633nm)" package="0805 [SMD]"]
  LED2 = smd LED [color="Red (633nm)" package="0805 [SMD]"]
  LED1 = smd LED [color="Red (633nm)" package="0805 [SMD]"]
  R3 = Resistor [tolerance=±5% resistance=68 package=THT]
  R1 = Resistor [tolerance=±5% resistance=68 package=THT]
  R2 = Resistor [tolerance=±5% resistance=68 package=THT]
  U2 = LuaNode32 / ESP32 [part_number=ESP32S-PIN30]
  IC1 = ULN2803A [package=THT]

nets:
  N1: LED3.cathode, R3.Pin_0
  N2: LED3.anode, IC1.Out_3
  N3: LED2.cathode, R2.Pin_0
  N4: LED2.anode, IC1.Out_2
  N5: LED1.cathode, R1.Pin_0
  N6: LED1.anode, IC1.Out_1
  N7: R3.Pin_1, R1.Pin_1, R2.Pin_1, U2.GND, IC1.0V
  N8: U2.D14, IC1.In_3
  N9: U2.D12, IC1.In_2
  N10: U2.D13, IC1.In_1
  N11: U2.Vin, IC1.COM_-_Common

custom parts:
  LuaNode32 / ESP32: New Image for LuaNode32 DOIT ESP32 DEVKIT V1. Base parts from LuaNode32 / ESP32 ESP32 based LuaNode32 by G.Noorlander DOIT Esp32 DevKit v1 (30 pins long, 11 pins width) by Werner Rothschopf (modified by vanepp Dec 2018)
